# Fritzing sketch RTPT (saved by Fritzing 0.9.3b)
breadboards: 1

parts:
  ARDUINO_MEGA_2560 = Arduino Mega 2560 (Rev3)
  ULBOX_GPS_MODULE = SUP500F [package=sup500f]
  3_5_Turn_Servo_(Pan/YAW/AZIMUTH) = Basic Servo
  180°_Servo_(Tillt/Elevation) = Basic Servo
  MPU-9250 = 9 Degrees of Freedom - Sensor Stick
  BAT1 = BC9VPC [package=bc9vpc]
  U1 = Voltage Regulator [package=to220-adj]
  PLANET_SELECTOR_POT = POT [package=alps_pot]
  MODE_SELECTOR_(NORMAL_/TRAJECTORY_) = Round Pushbutton

nets:
  N1: ARDUINO_MEGA_2560.A14, PLANET_SELECTOR_POT.S
  N2: ARDUINO_MEGA_2560.D21/SCL, ARDUINO_MEGA_2560.SCL, MPU-9250.SCL
  N3: ARDUINO_MEGA_2560.D20/SDA, MPU-9250.SDA
  N4: ARDUINO_MEGA_2560.D17_PWM/RX2, ULBOX_GPS_MODULE.TX-O
  N5: ARDUINO_MEGA_2560.D16_PWM/TX2, ULBOX_GPS_MODULE.RX-I
  GND: ARDUINO_MEGA_2560.GND, ULBOX_GPS_MODULE.GND, 3_5_Turn_Servo_(Pan/YAW/AZIMUTH).gnd, MPU-9250.GND, BAT1.V-, U1.IN, PLANET_SELECTOR_POT.A, MODE_SELECTOR_(NORMAL_/TRAJECTORY_).leg0
  N6: ARDUINO_MEGA_2560.D10_PWM, 180°_Servo_(Tillt/Elevation).pulse
  N7: ARDUINO_MEGA_2560.D9_PWM, 3_5_Turn_Servo_(Pan/YAW/AZIMUTH).pulse
  VCC: ARDUINO_MEGA_2560.VIN, ULBOX_GPS_MODULE.VCC, 3_5_Turn_Servo_(Pan/YAW/AZIMUTH).vcc, 180°_Servo_(Tillt/Elevation).vcc, U1.OUT
  5V: ARDUINO_MEGA_2560.5V, MPU-9250.VCC, PLANET_SELECTOR_POT.E
  N8: ARDUINO_MEGA_2560.D46, MODE_SELECTOR_(NORMAL_/TRAJECTORY_).leg1
  N9: BAT1.V+, U1.ADJ
